// Logisim project Divider_new_way.circ as structural Verilog: 5 circuits, main circuit Comparater
module main (
  input  A,
  input  A_2,
  input  A_3,
  input  A_4,
  input  B,
  input  B_2,
  input  B_3,
  input  B_4,
  output out_9
);

  Comparater Com (.B0(B_4), .A0(A_4), .B1(B_3), .A1(A_3), .B2(B_2), .A2(A_2), .B3(B), .A3(A), .out_9(out_9));
endmodule

module Comparater (
  input  B0,
  input  A0,
  input  B1,
  input  A1,
  input  B2,
  input  A2,
  input  B3,
  input  A3,
  output out_9
);

  wire nand_1_out, nand_2_out, nand_3_out, nand_4_out, not_1_out, not_2_out, not_3_out, not_4_out, xor_1_out,
       xor_2_out, xor_3_out, xor_4_out;

  xor xor_1 (xor_1_out, B0, A0);
  xor xor_2 (xor_2_out, B1, A1);
  xor xor_3 (xor_3_out, B2, A2);
  xor xor_4 (xor_4_out, B3, A3);
  not not_1 (not_1_out, A0);
  not not_2 (not_2_out, A1);
  not not_3 (not_3_out, A2);
  not not_4 (not_4_out, A3);
  nand nand_1 (nand_1_out, B0, xor_1_out, not_1_out);
  nand nand_2 (nand_2_out, B1, xor_2_out, not_2_out);
  nand nand_3 (nand_3_out, B2, xor_3_out, not_3_out);
  nand nand_4 (nand_4_out, B3, xor_4_out, not_4_out);
  and and_1 (out_9, nand_1_out, nand_2_out, nand_3_out, nand_4_out);
endmodule

module CompCounter (
  input  I0,
  input  Clear,
  output Q0,
  output Q1,
  output Q2
);

  wire d_ff_1_q, d_ff_2_qn, d_ff_3_qn, d_ff_4_qn, xor_1_out;

  D_Flip_Flop #(.trigger("high")) d_ff_1 (.clk(1'b1), .D(I0), .Q(d_ff_1_q), .en(xor_1_out));  // open: Qn, preset, reset
  xor xor_1 (xor_1_out, I0, d_ff_1_q);
  D_Flip_Flop d_ff_2 (
    .clk(xor_1_out), .D(d_ff_2_qn), .Q(Q0), .Qn(d_ff_2_qn), .en(1'b1), .reset(Clear));  // open: preset
  D_Flip_Flop d_ff_3 (
    .clk(d_ff_2_qn), .D(d_ff_3_qn), .Q(Q1), .Qn(d_ff_3_qn), .en(1'b1), .reset(Clear));  // open: preset
  D_Flip_Flop d_ff_4 (
    .clk(d_ff_3_qn), .D(d_ff_4_qn), .Q(Q2), .Qn(d_ff_4_qn), .en(1'b1), .reset(Clear));  // open: preset
endmodule

module _4_bit_CompCounter (
  input  I0,
  input  I1,
  input  I2,
  input  I3,
  input  Clear
);

  CompCounter compcounter_1 (.I0(I0), .Clear(Clear));  // open: Q0, Q1, Q2
  CompCounter compcounter_2 (.I0(I1), .Clear(Clear));  // open: Q0, Q1, Q2
  CompCounter compcounter_3 (.I0(I2), .Clear(Clear));  // open: Q0, Q1, Q2
  CompCounter compcounter_4 (.I0(I3), .Clear(Clear));  // open: Q0, Q1, Q2
endmodule

module TEST (
  input  I0,
  input  I1,
  input  I2,
  input  Clear,
  input  I3,
  output Q0,
  output Q1,
  output Q2
);

  wire adder_1_cout, adder_2_cout, d_ff_1_q, d_ff_1_qn, d_ff_2_q, d_ff_2_qn, d_ff_3_q, d_ff_3_qn, d_ff_4_q,
       d_ff_4_qn, d_ff_5_q, d_ff_5_qn, d_ff_6_q, d_ff_6_qn, d_ff_7_q, d_ff_7_qn, d_ff_8_q, d_ff_8_qn,
       d_ff_9_q, d_ff_9_qn, d_ff_10_q, d_ff_10_qn, xor_1_out, xor_2_out, xor_3_out, xor_4_out;

  D_Flip_Flop #(.trigger("high")) d_ff_1 (
    .clk(1'b1), .D(I0), .Q(d_ff_1_q), .Qn(d_ff_1_qn), .en(xor_1_out));  // open: preset, reset
  D_Flip_Flop #(.trigger("high")) d_ff_2 (
    .clk(1'b1), .D(I1), .Q(d_ff_2_q), .Qn(d_ff_2_qn), .en(xor_2_out));  // open: preset, reset
  D_Flip_Flop #(.trigger("high")) d_ff_3 (
    .clk(1'b1), .D(I2), .Q(d_ff_3_q), .Qn(d_ff_3_qn), .en(xor_3_out));  // open: preset, reset
  D_Flip_Flop #(.trigger("high")) d_ff_4 (
    .clk(1'b1), .D(I3), .Q(d_ff_4_q), .Qn(d_ff_4_qn), .en(xor_4_out));  // open: preset, reset
  xor xor_1 (xor_1_out, I0, d_ff_1_q);
  xor xor_2 (xor_2_out, I1, d_ff_2_q);
  xor xor_3 (xor_3_out, I2, d_ff_3_q);
  xor xor_4 (xor_4_out, I3, d_ff_4_q);
  D_Flip_Flop d_ff_5 (
    .clk(d_ff_1_qn), .D(d_ff_5_qn), .Q(d_ff_5_q), .Qn(d_ff_5_qn), .en(1'b1), .reset(Clear));  // open: preset
  D_Flip_Flop d_ff_6 (
    .clk(d_ff_5_qn), .D(d_ff_6_qn), .Q(d_ff_6_q), .Qn(d_ff_6_qn), .en(1'b1), .reset(Clear));  // open: preset
  D_Flip_Flop d_ff_7 (
    .clk(d_ff_6_qn), .D(d_ff_7_qn), .Q(d_ff_7_q), .Qn(d_ff_7_qn), .en(1'b1), .reset(Clear));  // open: preset
  D_Flip_Flop d_ff_8 (
    .clk(d_ff_1_q), .D(d_ff_8_qn), .Q(d_ff_8_q), .Qn(d_ff_8_qn), .en(1'b1), .reset(Clear));  // open: preset
  D_Flip_Flop d_ff_9 (
    .clk(d_ff_8_qn), .D(d_ff_9_qn), .Q(d_ff_9_q), .Qn(d_ff_9_qn), .en(1'b1), .reset(Clear));  // open: preset
  D_Flip_Flop d_ff_10 (
    .clk(d_ff_9_qn), .D(d_ff_10_qn), .Q(d_ff_10_q), .Qn(d_ff_10_qn), .en(1'b1), .reset(Clear));  // open: preset
  Adder #(.width(1)) adder_1 (.a(d_ff_8_q), .b(d_ff_5_q), .out(Q0), .cout(adder_1_cout));  // open: cin
  Adder #(.width(1)) adder_2 (.a(d_ff_9_q), .b(d_ff_6_q), .out(Q1), .cin(adder_1_cout), .cout(adder_2_cout));
  Adder #(.width(1)) adder_3 (.a(d_ff_10_q), .b(d_ff_7_q), .out(Q2), .cin(adder_2_cout));  // open: cout
endmodule
